# Fritzing sketch Intrremot_NodeMcu (saved by Fritzing 0.9.3b)
breadboards: 1

parts:
  U1 = NodeMCU V1.0
  R1 = Resistor [tolerance=±5% resistance=100 package=THT]
  LED1 = LED - 5mm [color="Red (633nm)" package="5 mm [THT]"]
  R2 = Resistor [tolerance=±5% resistance=100 package=THT]
  LED2 = LED - 5mm [color="Blue (430nm)" package="5 mm [THT]"]

nets:
  N1: U1.GND, R1.Pin_1, R2.Pin_1
  N2: U1.D5, LED2.anode
  N3: U1.D7, LED1.anode
  N4: R1.Pin_0, LED1.cathode
  N5: R2.Pin_0, LED2.cathode

custom parts:
  NodeMCU V1.0: ESP8266 based NodeMCU
